// Logisim project Lab7.circ as structural Verilog: 3 circuits, main circuit ParityGenerator
module XOR (
  input  X,
  input  Y,
  input  X_2,
  input  Y_2,
  output out_5,
  output out_6
);

  wire and_1_out, and_3_out, and_4_out, not_1_out, not_2_out, not_3_out, or_1_out;

  not not_1 (not_1_out, X_2);
  not not_2 (not_2_out, and_1_out);
  and and_1 (and_1_out, Y, X);
  or or_1 (or_1_out, Y, X);
  not not_3 (not_3_out, Y_2);
  and and_2 (out_5, not_2_out, or_1_out);
  and and_3 (and_3_out, not_3_out, X_2);
  and and_4 (and_4_out, Y_2, not_1_out);
  or or_2 (out_6, and_3_out, and_4_out);

  // Notes on the sheet:
  //   x XOR y = (x or y) and not (x and y)
  //   Minterm Expansion
  //   Both circuits are equivalent and valid representations of x XOR y
endmodule

module MyXOR (
  input  X,
  input  Y,
  output out_3
);

  wire and_1_out, and_2_out, not_1_out, not_2_out;

  not not_1 (not_1_out, X);
  not not_2 (not_2_out, Y);
  and and_1 (and_1_out, not_1_out, Y);
  and and_2 (and_2_out, X, not_2_out);
  or or_1 (out_3, and_1_out, and_2_out);

  // Notes on the sheet:
  //   Practice using Logism by recreating one of the implementations from XOR!
endmodule

module ParityGenerator (
  input  X,
  input  Y,
  input  Z,
  output Parity
);

  wire and_1_out, and_2_out, and_3_out, and_4_out, not_1_out, not_2_out, not_3_out, not_4_out, not_5_out,
       not_6_out;

  not not_1 (not_1_out, Y);
  not not_2 (not_2_out, Z);
  and and_1 (and_1_out, X, not_1_out, not_2_out);
  not not_3 (not_3_out, Z);
  not not_4 (not_4_out, X);
  and and_2 (and_2_out, not_4_out, Y, not_3_out);
  not not_5 (not_5_out, X);
  or or_1 (Parity, and_1_out, and_2_out, and_3_out, and_4_out);
  not not_6 (not_6_out, Y);
  and and_3 (and_3_out, not_5_out, not_6_out, Z);
  and and_4 (and_4_out, X, Y, Z);

  // Notes on the sheet:
  //   Input Bits
  //   Output Bit
  //   Write your parity circuit here
  //   the output = 1 if an odd number of inputs (1 or 3) are 1, otherwise 0
  //   ONLY use: NOT, AND, OR, and any custom functions you write (included in the .circ submission)
  //   WRITE YOUR NAME AND PLEDGE SOMEWHERE IN THIS CIRCUIT
  //   I pledge my honor that I have abided by the Stevens Honor System
  //   Shreyas Keerthi
endmodule
